// Logisim project DSDGroupProject.circ as structural Verilog: 15 circuits, main circuit main
module main (
  input  Ce,
  input  Cx,
  input  R
);

  wire clock_1_out, LeSelector_green, LeSelector_red, LeSelector_yellow, LxSelector_green, LxSelector_red,
       LxSelector_yellow, SegDecoder_out_5, SegDecoder_out_6, SegDecoder_out_7, SegDecoder_out_8,
       SegDecoder_out_9, SegDecoder_out_10, SegDecoder_out_11, trafficcontroller_1_la_0,
       trafficcontroller_1_la_1, trafficcontroller_1_lb_0, trafficcontroller_1_lb_1;

  Clock clock_1 (.out(clock_1_out));
  TrafficController trafficcontroller_1 (
    .LA_0(trafficcontroller_1_la_0), .LB_1(trafficcontroller_1_lb_1), .LB_0(trafficcontroller_1_lb_0),
    .LA_1(trafficcontroller_1_la_1), .R(R), .CLK(clock_1_out), .Ce(Ce), .Cx(Cx));
  LightSelector LxSelector (
    .Red(LxSelector_red), .Yellow(LxSelector_yellow), .Green(LxSelector_green),
    .L_1(trafficcontroller_1_lb_1), .L_0(trafficcontroller_1_lb_0));
  LED led_1 (.in(LeSelector_red));
  LightSelector LeSelector (
    .Red(LeSelector_red), .Yellow(LeSelector_yellow), .Green(LeSelector_green),
    .L_1(trafficcontroller_1_la_1), .L_0(trafficcontroller_1_la_0));
  LED led_2 (.in(LeSelector_yellow));
  LED led_3 (.in(LeSelector_green));
  Seg7 SegDecoder (
    .in_1(Ce), .out_5(SegDecoder_out_5), .out_6(SegDecoder_out_6), .out_7(SegDecoder_out_7),
    .out_8(SegDecoder_out_8), .out_9(SegDecoder_out_9), .out_10(SegDecoder_out_10), .out_11(SegDecoder_out_11));  // open: in_2, in_3, in_4
  LED led_4 (.in(LxSelector_red));
  LED led_5 (.in(LxSelector_yellow));
  LED led_6 (.in(LxSelector_green));
  _7_Segment_Display u_7_segment_display_1 (
    .g(SegDecoder_out_11), .f(SegDecoder_out_10), .a(SegDecoder_out_5), .b(SegDecoder_out_6),
    .e(SegDecoder_out_8), .d(SegDecoder_out_9), .c(SegDecoder_out_7));  // open: dp
endmodule

module SRLatch (
  input  R,
  input  S,
  output Q,
  output Q1
);

  nor nor_1 (Q, R, Q1);
  nor nor_2 (Q1, Q, S);
endmodule

module DLatch (
  input  CLK,
  input  D,
  output Q,
  output out_4
);

  wire and_1_out, and_2_out, not_1_out;

  not not_1 (not_1_out, D);
  and and_1 (and_1_out, CLK, not_1_out);
  and and_2 (and_2_out, CLK, D);
  SRLatch srlatch_1 (.Q1(out_4), .Q(Q), .S(and_2_out), .R(and_1_out));
endmodule

module DFlipFlop (
  input  CLK,
  input  D,
  output Q,
  output out_4
);

  wire dlatch_1_q, not_1_out;

  not not_1 (not_1_out, CLK);
  DLatch dlatch_1 (.Q(dlatch_1_q), .D(D), .CLK(not_1_out));  // open: out_4
  DLatch dlatch_2 (.out_4(out_4), .Q(Q), .D(dlatch_1_q), .CLK(CLK));
endmodule

module FourBitRegister (
  input  in_1,
  input  [3:0] D,
  output [3:0] Q
);

  DFlipFlop dflipflop_1 (.Q(Q[0]), .CLK(in_1), .D(D[0]));  // open: out_4
  DFlipFlop dflipflop_2 (.Q(Q[1]), .CLK(in_1), .D(D[1]));  // open: out_4
  DFlipFlop dflipflop_3 (.Q(Q[2]), .CLK(in_1), .D(D[2]));  // open: out_4
  DFlipFlop dflipflop_4 (.Q(Q[3]), .CLK(in_1), .D(D[3]));  // open: out_4
endmodule

module EnableFlipFlop (
  input  CLK,
  input  D,
  input  EN,
  output Q
);

  wire multiplexer_1_out;

  Multiplexer multiplexer_1 (.in0(Q), .in1(D), .out(multiplexer_1_out), .sel(EN));
  DFlipFlop dflipflop_1 (.Q(Q), .CLK(CLK), .D(multiplexer_1_out));  // open: out_4
endmodule

module ResettableFlipFlop (
  input  in_1,
  input  D,
  input  R,
  output Q
);

  wire and_1_out, not_1_out;

  and and_1 (and_1_out, D, not_1_out);
  not not_1 (not_1_out, R);
  DFlipFlop dflipflop_1 (.Q(Q), .CLK(in_1), .D(and_1_out));  // open: out_4
endmodule

module TwoBitRegister (
  input  CLK,
  input  D_0,
  input  D_1,
  output Q_0,
  output Q_1
);

  DFlipFlop dflipflop_1 (.Q(Q_0), .CLK(CLK), .D(D_0));  // open: out_4
  DFlipFlop dflipflop_2 (.Q(Q_1), .CLK(CLK), .D(D_1));  // open: out_4
endmodule

module StateRegister (
  input  CLK,
  input  D_1,
  input  D_2,
  input  R,
  output Q_1,
  output Q_2
);

  wire and_1_out, and_2_out, not_1_out;

  and and_1 (and_1_out, D_1, not_1_out);
  and and_2 (and_2_out, D_2, not_1_out);
  not not_1 (not_1_out, R);
  DFlipFlop dflipflop_1 (.Q(Q_1), .CLK(CLK), .D(and_1_out));  // open: out_4
  DFlipFlop dflipflop_2 (.Q(Q_2), .CLK(CLK), .D(and_2_out));  // open: out_4
endmodule

module TrafficController (
  input  CLK,
  input  Ce,
  input  R,
  input  Cx,
  output LA_1,
  output LA_0,
  output LB_1,
  output LB_0
);

  wire and_1_out, and_2_out, or_1_out, stateregister_1_q_2, xor_1_out;

  xor xor_1 (xor_1_out, LA_1, stateregister_1_q_2);
  and and_1 (and_1_out, ~LA_1, ~stateregister_1_q_2, ~Ce);  // AND_Gate
  and and_2 (and_2_out, LA_1, ~stateregister_1_q_2, ~Cx);  // AND_Gate
  or or_1 (or_1_out, and_1_out, and_2_out);
  StateRegister stateregister_1 (
    .Q_1(LA_1), .Q_2(stateregister_1_q_2), .CLK(CLK), .R(R), .D_1(xor_1_out), .D_2(or_1_out));
  and and_3 (LA_0, ~LA_1, stateregister_1_q_2);  // AND_Gate
  not not_1 (LB_1, LA_1);
  and and_4 (LB_0, LA_1, stateregister_1_q_2);
endmodule

module LightSelector (
  input  L_0,
  input  L_1,
  output Red,
  output Yellow,
  output Green
);

  wire not_1_out, not_2_out;

  not not_1 (not_1_out, L_1);
  not not_2 (not_2_out, L_0);
  and and_1 (Red, L_1, not_2_out);
  and and_2 (Yellow, not_1_out, L_0);
  and and_3 (Green, not_1_out, not_2_out);
endmodule

module DivideBy3OneHotEncoding (
  input  in_1
);

  wire clock_1_out, S1_q, S2_q, settableflipflop_1_q;

  Clock clock_1 (.out(clock_1_out));
  ResettableFlipFlop S1 (.Q(S1_q), .in_1(clock_1_out), .D(settableflipflop_1_q), .R(in_1));
  ResettableFlipFlop S2 (.Q(S2_q), .in_1(clock_1_out), .D(S1_q), .R(in_1));
  SettableFlipFlop settableflipflop_1 (.Q(settableflipflop_1_q), .CLK(clock_1_out), .D(S2_q), .S(in_1));
  LED led_1 (.in(settableflipflop_1_q));
endmodule

module SettableFlipFlop (
  input  CLK,
  input  D,
  input  S,
  output Q
);

  wire or_1_out;

  or or_1 (or_1_out, D, S);
  DFlipFlop dflipflop_1 (.Q(Q), .CLK(CLK), .D(or_1_out));  // open: out_4
endmodule

module CrossCoupledInverter (
  input  in_1,
  input  in_2
);

  not not_1 (in_1, in_2);
  not not_2 (in_2, in_1);
endmodule

module Seg7 (
  input  in_1,
  input  in_2,
  input  in_3,
  input  in_4,
  output out_5,
  output out_6,
  output out_7,
  output out_8,
  output out_9,
  output out_10,
  output out_11
);

  wire and_1_out, and_2_out, and_3_out, and_4_out, and_5_out, and_6_out, and_7_out, and_8_out, and_9_out,
       and_10_out, and_11_out, and_12_out, and_13_out, and_14_out, and_15_out, and_16_out, and_17_out,
       and_18_out, not_1_out, not_2_out, not_3_out, not_4_out;

  not not_1 (not_1_out, in_4);
  not not_2 (not_2_out, in_3);
  not not_3 (not_3_out, in_2);
  not not_4 (not_4_out, in_1);
  and and_1 (and_1_out, not_1_out, in_2);
  and and_2 (and_2_out, not_1_out, in_3, in_1);
  and and_3 (and_3_out, in_4, not_2_out, not_3_out);
  and and_4 (and_4_out, not_2_out, not_3_out, not_4_out);
  and and_5 (and_5_out, not_1_out, not_2_out);
  and and_6 (and_6_out, not_2_out, not_3_out);
  and and_7 (and_7_out, not_1_out, in_2, in_1);
  and and_8 (and_8_out, not_1_out, not_3_out, not_4_out);
  and and_9 (and_9_out, not_1_out, in_1);
  and and_10 (and_10_out, not_2_out, not_3_out);
  and and_11 (and_11_out, not_1_out, in_3);
  and and_12 (and_12_out, not_1_out, in_3, not_3_out, in_1);
  and and_13 (and_13_out, not_2_out, not_3_out, not_4_out);
  and and_14 (and_14_out, not_1_out, not_2_out, in_2);
  and and_15 (and_15_out, not_1_out, in_2, not_4_out);
  and and_16 (and_16_out, not_1_out, in_3, not_4_out);
  and and_17 (and_17_out, not_1_out, in_3, not_3_out);
  and and_18 (and_18_out, not_1_out, in_2, not_4_out);
  or a (out_5, and_1_out, and_2_out, and_3_out, and_4_out);
  or b (out_6, and_5_out, and_6_out, and_7_out, and_8_out);
  or c (out_7, and_9_out, and_10_out, and_11_out);
  or d (out_8, and_12_out, and_13_out, and_14_out, and_15_out, and_3_out);
  or e (out_9, and_15_out, and_13_out);
  or f (out_10, and_13_out, and_16_out, and_3_out, and_17_out);
  or g (out_11, and_14_out, and_18_out, and_17_out, and_3_out);
endmodule
